// Logisim project cpu-8-bit.circ as structural Verilog: 8 circuits, main circuit main
module main (
  input  in_1,
  output [7:0] out_2,
  output [7:0] out_3
);

  wire A_q, alu_1_a_larger, alu_1_carry_out, alu_1_equal, alu_1_zero, C_q, clock_1_out, controlunit_1_acc_e,
       controlunit_1_acc_s, controlunit_1_flags_s, controlunit_1_iar_e, controlunit_1_iar_s,
       controlunit_1_ir_s, controlunit_1_mar_s, controlunit_1_r0_e, controlunit_1_r0_s, controlunit_1_r1_e,
       controlunit_1_r1_s, controlunit_1_r2_e, controlunit_1_r2_s, controlunit_1_r3_e, controlunit_1_r3_s,
       controlunit_1_ram_e, controlunit_1_ram_s, controlunit_1_tmp_s, E_q, not_1_out, Z_q;
  wire [0:0] controlunit_1_bus_1;
  wire [2:0] controlunit_1_op;
  wire [7:0] ACC_q, alu_1_c, controlled_buffer_1_out, controlled_buffer_2_out, controlled_buffer_3_out,
       IAR_q, IR_q, or_1_out, R_q, ram_1_data, register_1_q, register_3_q, register_4_q, register_5_q,
       register_6_q, TMP_q;

  Clock clock_1 (.out(clock_1_out));
  not not_1 (not_1_out, in_1);
  assign controlled_buffer_1_out = 1'b1 ? controlled_buffer_3_out : 8'bz;  // Controlled_Buffer controlled_buffer_1
  Register #(.trigger("high")) register_1 (.D(controlled_buffer_3_out), .Q(register_1_q), .clk(1'b1));  // open: en, clr
  Register #(.trigger("high")) register_2 (.D(or_1_out), .Q(out_3), .clk(1'b1));  // open: en, clr
  ALU alu_1 (
    .a(register_1_q), .b(out_3), .carry_in(C_q), .op(controlunit_1_op), .a_larger(alu_1_a_larger),
    .equal(alu_1_equal), .zero(alu_1_zero), .c(alu_1_c), .carry_out(alu_1_carry_out));
  assign controlled_buffer_2_out = 1'b1 ? alu_1_c : 8'bz;  // Controlled_Buffer controlled_buffer_2
  assign controlled_buffer_3_out = controlunit_1_acc_e ? ACC_q : 8'bz;  // Controlled_Buffer controlled_buffer_3
  Register #(.trigger("high")) ACC (
    .D(controlled_buffer_2_out), .Q(ACC_q), .clk(controlunit_1_acc_s));  // open: en, clr
  Register #(.trigger("high")) TMP (
    .D(controlled_buffer_1_out), .Q(TMP_q), .clk(controlunit_1_tmp_s));  // open: en, clr
  assign or_1_out = TMP_q | {{7{1'b0}}, controlunit_1_bus_1[0]};  // OR_Gate or_1, 8 bits wide
  Register #(.width(1), .trigger("high")) C (
    .D(alu_1_carry_out), .Q(C_q), .clk(controlunit_1_flags_s), .clr(not_1_out));  // open: en
  Register #(.width(1), .trigger("high")) A (
    .D(alu_1_a_larger), .Q(A_q), .clk(controlunit_1_flags_s), .clr(not_1_out));  // open: en
  Register #(.width(1), .trigger("high")) E (
    .D(alu_1_equal), .Q(E_q), .clk(controlunit_1_flags_s), .clr(not_1_out));  // open: en
  Register #(.width(1), .trigger("high")) Z (
    .D(alu_1_zero), .Q(Z_q), .clk(controlunit_1_flags_s), .clr(not_1_out));  // open: en
  Register #(.trigger("high")) register_3 (
    .D(controlled_buffer_3_out), .en(controlunit_1_r0_e), .Q(register_3_q), .clk(controlunit_1_r0_s));  // open: clr
  ControlUnit controlunit_1 (
    .start(in_1), .C(C_q), .A(A_q), .E(E_q), .Z(Z_q), .IAR_s(controlunit_1_iar_s),
    .IAR_e(controlunit_1_iar_e), .IR_s(controlunit_1_ir_s), .IR_data(IR_q), .bus_1(controlunit_1_bus_1[0]),
    .op(controlunit_1_op), .R0_s(controlunit_1_r0_s), .R0_e(controlunit_1_r0_e), .R1_e(controlunit_1_r1_e),
    .R2_s(controlunit_1_r2_s), .R2_e(controlunit_1_r2_e), .R3_s(controlunit_1_r3_s),
    .R3_e(controlunit_1_r3_e), .R1_s(controlunit_1_r1_s), .MAR_s(controlunit_1_mar_s),
    .RAM_s(controlunit_1_ram_s), .RAM_e(controlunit_1_ram_e), .ACC_s(controlunit_1_acc_s),
    .ACC_e(controlunit_1_acc_e), .TMP_s(controlunit_1_tmp_s), .Flags_s(controlunit_1_flags_s),
    .clock(clock_1_out));  // open: IO_clk_e, IO_clk_s, Data_Address, Input_Output
  assign controlled_buffer_3_out = controlunit_1_r0_e ? register_3_q : 8'bz;  // Controlled_Buffer controlled_buffer_4
  Register #(.trigger("high")) register_4 (
    .D(controlled_buffer_3_out), .en(controlunit_1_r1_e), .Q(register_4_q), .clk(controlunit_1_r1_s));  // open: clr
  Register #(.trigger("high")) IAR (
    .D(controlled_buffer_3_out), .Q(IAR_q), .clk(controlunit_1_iar_s), .clr(not_1_out));  // open: en
  // Probe on controlled_buffer_3_out
  assign controlled_buffer_3_out = controlunit_1_r1_e ? register_4_q : 8'bz;  // Controlled_Buffer controlled_buffer_5
  Register #(.trigger("high")) register_5 (
    .D(controlled_buffer_3_out), .en(controlunit_1_r2_e), .Q(register_5_q), .clk(controlunit_1_r2_s));  // open: clr
  assign controlled_buffer_3_out = controlunit_1_iar_e ? IAR_q : 8'bz;  // Controlled_Buffer controlled_buffer_6
  assign controlled_buffer_3_out = controlunit_1_r2_e ? register_5_q : 8'bz;  // Controlled_Buffer controlled_buffer_7
  Register #(.trigger("high")) IR (.D(controlled_buffer_3_out), .Q(IR_q), .clk(controlunit_1_ir_s));  // open: en, clr
  assign controlled_buffer_3_out = controlunit_1_r3_e ? register_6_q : 8'bz;  // Controlled_Buffer controlled_buffer_8
  Register #(.trigger("high")) register_6 (
    .D(controlled_buffer_3_out), .en(controlunit_1_r3_e), .Q(register_6_q), .clk(controlunit_1_r3_s));  // open: clr
  assign out_2 = 1'b1 ? controlled_buffer_3_out : 8'bz;  // Controlled_Buffer controlled_buffer_9
  Register #(.trigger("high")) R (.D(out_2), .Q(R_q), .clk(controlunit_1_mar_s));  // open: en, clr
  RAM_part ram_1 (
    .addr(R_q), .data(ram_1_data), .clk(controlunit_1_ram_s), .ld(controlunit_1_ram_e));  // open: sel, clr
  assign ram_1_data = controlunit_1_ram_s ? controlled_buffer_3_out : 8'bz;  // Controlled_Buffer controlled_buffer_10
  assign controlled_buffer_3_out = controlunit_1_ram_e ? ram_1_data : 8'bz;  // Controlled_Buffer controlled_buffer_11
  Pull_Resistor pull_resistor_1 (.node(controlled_buffer_3_out));
endmodule

module Stepper (
  input  reset,
  input  clock,
  output _1,
  output _2,
  output _3,
  output _4,
  output _5,
  output _6,
  output _7
);

  wire memory_1_bit_1_output, memory_1_bit_2_output, memory_1_bit_3_output, memory_1_bit_4_output,
       memory_1_bit_5_output, memory_1_bit_6_output, memory_1_bit_7_output, memory_1_bit_8_output,
       memory_1_bit_9_output, memory_1_bit_10_output, memory_1_bit_12_output, not_1_out, not_2_out,
       not_3_out, not_4_out, not_5_out, not_6_out, not_7_out, not_8_out, or_1_out, or_2_out;

  not not_1 (not_1_out, clock);
  not not_2 (not_2_out, reset);
  or or_1 (or_1_out, reset, not_1_out);
  or or_2 (or_2_out, reset, clock);
  or or_3 (_1, reset, not_3_out);
  Memory_1_bit memory_1_bit_1 (.\input (not_2_out), .s(or_1_out), .\output (memory_1_bit_1_output));
  not not_3 (not_3_out, memory_1_bit_2_output);
  Memory_1_bit memory_1_bit_2 (.\input (memory_1_bit_1_output), .s(or_2_out), .\output (memory_1_bit_2_output));
  and and_1 (_2, memory_1_bit_2_output, not_4_out);
  not not_4 (not_4_out, memory_1_bit_4_output);
  Memory_1_bit memory_1_bit_3 (.\input (memory_1_bit_2_output), .s(or_1_out), .\output (memory_1_bit_3_output));
  Memory_1_bit memory_1_bit_4 (.\input (memory_1_bit_3_output), .s(or_2_out), .\output (memory_1_bit_4_output));
  and and_2 (_3, memory_1_bit_4_output, not_5_out);
  Memory_1_bit memory_1_bit_5 (.\input (memory_1_bit_4_output), .s(or_1_out), .\output (memory_1_bit_5_output));
  not not_5 (not_5_out, memory_1_bit_6_output);
  Memory_1_bit memory_1_bit_6 (.\input (memory_1_bit_5_output), .s(or_2_out), .\output (memory_1_bit_6_output));
  and and_3 (_4, memory_1_bit_6_output, not_6_out);
  not not_6 (not_6_out, memory_1_bit_7_output);
  Memory_1_bit memory_1_bit_7 (.\input (memory_1_bit_8_output), .s(or_2_out), .\output (memory_1_bit_7_output));
  Memory_1_bit memory_1_bit_8 (.\input (memory_1_bit_6_output), .s(or_1_out), .\output (memory_1_bit_8_output));
  and and_4 (_5, memory_1_bit_7_output, not_7_out);
  Memory_1_bit memory_1_bit_9 (.\input (memory_1_bit_7_output), .s(or_1_out), .\output (memory_1_bit_9_output));
  not not_7 (not_7_out, memory_1_bit_10_output);
  Memory_1_bit memory_1_bit_10 (.\input (memory_1_bit_9_output), .s(or_2_out), .\output (memory_1_bit_10_output));
  and and_5 (_6, memory_1_bit_10_output, not_8_out);
  not not_8 (not_8_out, _7);
  Memory_1_bit memory_1_bit_11 (.\input (memory_1_bit_12_output), .s(or_2_out), .\output (_7));
  Memory_1_bit memory_1_bit_12 (.\input (memory_1_bit_10_output), .s(or_1_out), .\output (memory_1_bit_12_output));
endmodule

module Memory_1_bit (
  input  \input ,
  input  s,
  output \output 
);

  wire _1_out, _2_out, _4_out;

  nand _1 (_1_out, \input , s);
  nand _2 (_2_out, _1_out, s);
  nand _3 (\output , _1_out, _4_out);
  nand _4 (_4_out, \output , _2_out);
endmodule

module ControlUnit (
  input  start,
  input  clock,
  input  C,
  input  A,
  input  E,
  input  Z,
  input  [7:0] IR_data,
  output IR_s,
  output bus_1,
  output MAR_s,
  output IAR_e,
  output IAR_s,
  output RAM_e,
  output ACC_s,
  output ACC_e,
  output RAM_s,
  output IO_clk_e,
  output TMP_s,
  output Flags_s,
  output IO_clk_s,
  output R0_s,
  output R1_s,
  output R0_e,
  output R2_s,
  output R1_e,
  output R3_s,
  output R2_e,
  output R3_e,
  output Data_Address,
  output Input_Output,
  output [2:0] op
);

  wire A_out, ACC_e_out, ACC_s_out, ALU_2_out, ALU_3_out, ALU_out, and_5_out, and_6_out, and_7_out,
       and_8_out, and_9_out, and_10_out, and_11_out, and_12_out, and_16_out, and_17_out, C_out, clr_2_out,
       CLR_out, data_2_out, data_3_out, data_4_out, data_out, decoder_1_out0, decoder_1_out1, decoder_1_out2,
       decoder_1_out3, decoder_2_out0, decoder_2_out1, decoder_2_out2, decoder_2_out3, decoder_3_out0,
       decoder_3_out1, decoder_3_out2, decoder_3_out3, decoder_3_out4, decoder_3_out5, decoder_3_out6,
       decoder_3_out7, decoder_4_out0, decoder_4_out1, decoder_4_out2, decoder_4_out3, E_out, Flags_s_out,
       i_o_2_out, i_o_3_out, I_O_out, IAR_e_out, IAR_s_out, jmpif_2_out, jmpif_3_out, jmpif_4_out, JMPIF_out,
       jmpr_2_out, jmpr_3_out, JMPR_out, jump_2_out, jump_out, load_2_out, load_3_out, load_out, MAR_s_out,
       not_1_out, not_2_out, not_3_out, not_4_out, or_5_out, or_6_out, RAM_e_out, RegA_e_out, RegB_e_out,
       RegB_s_out, register_1_q, stepper_1__1, stepper_1__2, stepper_1__3, stepper_1__4, stepper_1__5,
       stepper_1__6, stepper_1__7, store_2_out, store_3_out, store_out, Z_out;

  or or_1 (R0_e, and_5_out, and_9_out);
  or or_2 (R1_e, and_6_out, and_10_out);
  or or_3 (R2_e, and_7_out, and_11_out);
  or or_4 (R3_e, and_8_out, and_12_out);
  and and_1 (IAR_e, clock, IAR_e_out);
  and and_2 (RAM_e, clock, RAM_e_out);
  and and_3 (ACC_e, clock, ACC_e_out);
  and and_4 (IO_clk_e, clock, i_o_3_out);
  and and_5 (and_5_out, clock, RegB_e_out, decoder_1_out0);
  and and_6 (and_6_out, clock, RegB_e_out, decoder_1_out1);
  and and_7 (and_7_out, clock, RegB_e_out, decoder_1_out2);
  and and_8 (and_8_out, clock, RegB_e_out, decoder_1_out3);
  and and_9 (and_9_out, clock, RegA_e_out, decoder_2_out0);
  and and_10 (and_10_out, clock, RegA_e_out, decoder_2_out1);
  and and_11 (and_11_out, clock, RegA_e_out, decoder_2_out2);
  and and_12 (and_12_out, clock, RegA_e_out, decoder_2_out3);
  Register #(.width(1), .trigger("high")) register_1 (.D(start), .Q(register_1_q), .clk(clock));  // open: en, clr
  Decoder #(.select(2)) decoder_1 (
    .out0(decoder_1_out0), .out1(decoder_1_out1), .out2(decoder_1_out2), .out3(decoder_1_out3),
    .sel(IR_data[1:0]));  // open: en
  Decoder #(.select(2)) decoder_2 (
    .out0(decoder_2_out0), .out1(decoder_2_out1), .out2(decoder_2_out2), .out3(decoder_2_out3),
    .sel(IR_data[3:2]));  // open: en
  and and_13 (op[2], stepper_1__5, IR_data[7], IR_data[4]);
  and and_14 (op[1], stepper_1__5, IR_data[7], IR_data[5]);
  and and_15 (op[0], stepper_1__5, IR_data[7], IR_data[6]);
  and and_16 (and_16_out, start, register_1_q);
  or bus1 (bus_1, clr_2_out, stepper_1__1, data_2_out, jmpif_2_out);
  or u_IAR_e (IAR_e_out, stepper_1__1, data_2_out, jmpr_2_out, jmpif_2_out);
  or u_RAM_e (RAM_e_out, stepper_1__2, jmpif_4_out, jmpr_3_out, data_3_out, load_3_out);
  or u_ACC_e (ACC_e_out, stepper_1__3, jmpif_3_out, data_4_out, ALU_3_out);
  or RegB_e (RegB_e_out, ALU_out, store_3_out, jump_2_out, i_o_2_out);
  or RegA_e (RegA_e_out, load_2_out, store_2_out, ALU_2_out);
  Decoder #(.select(3)) decoder_3 (
    .out0(decoder_3_out0), .out1(decoder_3_out1), .out2(decoder_3_out2), .out3(decoder_3_out3),
    .out4(decoder_3_out4), .out5(decoder_3_out5), .out6(decoder_3_out6), .out7(decoder_3_out7),
    .sel(IR_data[6:4]));  // open: en
  not not_1 (not_1_out, IR_data[7]);
  not not_2 (not_2_out, and_16_out);
  Stepper stepper_1 (
    ._1(stepper_1__1), ._2(stepper_1__2), ._3(stepper_1__3), ._4(stepper_1__4), ._5(stepper_1__5),
    ._6(stepper_1__6), ._7(stepper_1__7), .reset(or_5_out), .clock(clock));
  and load (load_out, not_1_out, decoder_3_out0);
  and store (store_out, not_1_out, decoder_3_out1);
  and data (data_out, not_1_out, decoder_3_out2);
  and jump (jump_out, not_1_out, decoder_3_out3);
  and JMPR (JMPR_out, not_1_out, decoder_3_out4);
  and JMPIF (JMPIF_out, not_1_out, decoder_3_out5);
  and CLR (CLR_out, not_1_out, decoder_3_out6);
  and I_O (I_O_out, not_1_out, decoder_3_out7);
  and u_C (C_out, IR_data[3], C);
  and u_A (A_out, IR_data[2], A);
  and u_E (E_out, IR_data[1], E);
  and u_Z (Z_out, IR_data[0], Z);
  or or_5 (or_5_out, not_2_out, stepper_1__7);
  and ALU (ALU_out, stepper_1__4, IR_data[7]);
  and load_2 (load_2_out, stepper_1__4, load_out);
  buf store_2 (store_2_out, store_out);  // AND_Gate
  and data_2 (data_2_out, stepper_1__4, data_out);
  and jump_2 (jump_2_out, stepper_1__4, jump_out);
  and jmpr_2 (jmpr_2_out, stepper_1__4, JMPR_out);
  and jmpif_2 (jmpif_2_out, stepper_1__4, JMPIF_out);
  and clr_2 (clr_2_out, stepper_1__4, CLR_out);
  and i_o_2 (i_o_2_out, stepper_1__4, I_O_out, IR_data[3]);
  not not_3 (not_3_out, IR_data[3]);
  not not_4 (not_4_out, and_17_out);
  and and_17 (and_17_out, IR_data[4], IR_data[5], IR_data[6]);
  or or_6 (or_6_out, C_out, A_out, E_out, Z_out);
  and ALU_2 (ALU_2_out, stepper_1__5, IR_data[7]);
  and load_3 (load_3_out, stepper_1__5, load_out);
  and store_3 (store_3_out, stepper_1__5, store_out);
  and data_3 (data_3_out, stepper_1__5, data_out);
  and jmpr_3 (jmpr_3_out, stepper_1__5, JMPR_out);
  and jmpif_3 (jmpif_3_out, stepper_1__5, JMPIF_out);
  and i_o_3 (i_o_3_out, stepper_1__5, I_O_out, not_3_out);
  and ALU_3 (ALU_3_out, stepper_1__6, IR_data[7], not_4_out);
  and data_4 (data_4_out, stepper_1__6, data_out);
  and jmpif_4 (jmpif_4_out, stepper_1__6, JMPIF_out, or_6_out);
  or u_MAR_s (MAR_s_out, stepper_1__1, load_2_out, store_2_out, data_2_out, jmpr_2_out, jmpif_2_out);
  or u_IAR_s (IAR_s_out, stepper_1__3, jump_2_out, jmpr_3_out, data_4_out, jmpif_3_out, jmpif_4_out);
  or u_ACC_s (ACC_s_out, stepper_1__1, data_2_out, jmpif_2_out, ALU_2_out);
  or u_Flags_s (Flags_s_out, clr_2_out, ALU_2_out);
  or RegB_s (RegB_s_out, load_3_out, ALU_3_out, data_3_out, i_o_3_out);
  Decoder #(.select(2)) decoder_4 (
    .out0(decoder_4_out0), .out1(decoder_4_out1), .out2(decoder_4_out2), .out3(decoder_4_out3),
    .sel(IR_data[1:0]));  // open: en
  and and_18 (IR_s, clock, stepper_1__2);
  and and_19 (MAR_s, clock, MAR_s_out);
  and and_20 (IAR_s, clock, IAR_s_out);
  and and_21 (ACC_s, clock, ACC_s_out);
  and and_22 (RAM_s, clock, store_3_out);
  and and_23 (TMP_s, clock, ALU_out);
  and and_24 (Flags_s, clock, Flags_s_out);
  and i_o_clk (IO_clk_s, clock, i_o_2_out);
  and and_25 (R0_s, clock, RegB_s_out, decoder_4_out0);
  and and_26 (R1_s, clock, RegB_s_out, decoder_4_out1);
  and and_27 (R2_s, clock, RegB_s_out, decoder_4_out2);
  and and_28 (R3_s, clock, RegB_s_out, decoder_4_out3);

  assign Data_Address = IR_data[2];
  assign Input_Output = IR_data[3];

  // Notes on the sheet:
  //   All Enables
  //   step4
  //   step5
  //   step6
  //   All Sets
endmodule

module ALU (
  input  [7:0] a,
  input  [7:0] b,
  input  carry_in,
  input  [2:0] op,
  output a_larger,
  output equal,
  output zero,
  output [7:0] c,
  output carry_out
);

  wire decoder_1_out0, decoder_1_out1, decoder_1_out2, decoder_1_out3, decoder_1_out4, decoder_1_out5,
       decoder_1_out6;
  wire [7:0] adder_1_out, and_1_out, not_1_out, or_1_out, shifter_1_out, shifter_2_out, xor_1_out;

  assign xor_1_out = a ^ b;  // XOR_Gate xor_1, 8 bits wide
  assign or_1_out = a | b;  // OR_Gate or_1, 8 bits wide
  assign and_1_out = a & b;  // AND_Gate and_1, 8 bits wide
  assign not_1_out = ~a;  // NOT_Gate not_1, 8 bits wide
  Shifter shifter_1 (.in(a), .\dist (3'b001), .out(shifter_1_out));
  Shifter #(.shift("lr")) shifter_2 (.in(a), .\dist (3'b001), .out(shifter_2_out));
  Adder adder_1 (.a(b), .b(a), .out(adder_1_out), .cin(carry_in), .cout(carry_out));
  Decoder #(.select(3)) decoder_1 (
    .out0(decoder_1_out0), .out1(decoder_1_out1), .out2(decoder_1_out2), .out3(decoder_1_out3),
    .out4(decoder_1_out4), .out5(decoder_1_out5), .out6(decoder_1_out6), .sel(op));  // open: out7, en
  Comparator comparator_1 (.a(a), .b(b), .gt(a_larger), .eq(equal));  // open: lt
  assign c = decoder_1_out6 ? xor_1_out : 8'bz;  // Controlled_Buffer controlled_buffer_1
  assign c = decoder_1_out5 ? or_1_out : 8'bz;  // Controlled_Buffer controlled_buffer_2
  assign c = decoder_1_out4 ? and_1_out : 8'bz;  // Controlled_Buffer controlled_buffer_3
  assign c = decoder_1_out3 ? not_1_out : 8'bz;  // Controlled_Buffer controlled_buffer_4
  assign c = decoder_1_out2 ? shifter_1_out : 8'bz;  // Controlled_Buffer controlled_buffer_5
  assign c = decoder_1_out1 ? shifter_2_out : 8'bz;  // Controlled_Buffer controlled_buffer_6
  assign c = decoder_1_out0 ? adder_1_out : 8'bz;  // Controlled_Buffer controlled_buffer_7
  Comparator comparator_2 (.a({8{1'b0}}), .b(c), .eq(zero));  // open: gt, lt
endmodule

module RAM (
  input  [7:0] in_1,
  input  [7:0] address,
  input  Clk,
  input  load_store
);

  wire not_1_out;
  wire [7:0] controlled_buffer_1_out;

  assign controlled_buffer_1_out = load_store ? in_1 : 8'bz;  // Controlled_Buffer controlled_buffer_1
  not not_1 (not_1_out, load_store);
  RAM_part ram_1 (.addr(address), .data(controlled_buffer_1_out), .clk(Clk), .ld(not_1_out));  // open: sel, clr
endmodule

module ShifterL (
  input  shift_in,
  input  _7,
  input  _6,
  input  _5,
  input  _4,
  input  _3,
  input  _2,
  input  _1,
  input  _0,
  output _7_2,
  output _6_2,
  output _5_2,
  output _4_2,
  output _3_2,
  output _2_2,
  output _1_2,
  output _0_2,
  output shift_out
);


  assign _0_2 = _1;
  assign _1_2 = _2;
  assign _2_2 = _3;
  assign _3_2 = _4;
  assign _4_2 = _5;
  assign _5_2 = _6;
  assign _6_2 = _7;
  assign _7_2 = shift_in;
  assign shift_out = _0;
endmodule

module ShifterR (
  input  _7,
  input  _6,
  input  _5,
  input  _4,
  input  _3,
  input  _2,
  input  _1,
  input  _0,
  input  shift_in,
  output shift_out,
  output _7_2,
  output _6_2,
  output _5_2,
  output _4_2,
  output _3_2,
  output _2_2,
  output _1_2,
  output _0_2
);


  assign _0_2 = shift_in;
  assign _1_2 = _0;
  assign _2_2 = _1;
  assign _3_2 = _2;
  assign _4_2 = _3;
  assign _5_2 = _4;
  assign _6_2 = _5;
  assign _7_2 = _6;
  assign shift_out = _7;
endmodule
